# Fritzing sketch cardiodog sketch (saved by Fritzing 0.9.3b)
breadboards: 1

parts:
  Componente1 = Arduino Uno (Rev3)
  LED1 = LED - 5mm [color="Red (633nm)" package="5 mm [THT]"]
  SEN1 = Pulse Sensor [package=SIP-3]
  U1 = LCD-16X2 [package=lcd-16x2_noholes]
  U2 = POT [package=pot_mammoth]

nets:
  N1: Componente1.A0, SEN1.GND
  N2: Componente1.D11_PWM/MOSI, U1.E
  N3: Componente1.D12/MISO, U1.RS
  N4: Componente1.D13/SCK, LED1.anode
  GND: Componente1.GND, LED1.cathode, SEN1.Signal, U1.VSS, U1.R_W, U1.K
  N5: Componente1.D2, U1.DB7
  N6: Componente1.D3_PWM, U1.DB6
  N7: Componente1.D4, U1.DB5
  N8: Componente1.D5_PWM, U1.DB4
  5V: Componente1.5V, SEN1.VCC, U1.VDD, U1.A, U2.S
  N9: U1.VO, U2.A

custom parts:
  Pulse Sensor: Pulse Sensor Optical Heart Beat Sensor
